# Fritzing sketch circuito (saved by Fritzing 0.9.3b)

parts:
  Raspberry_Pi_B_rev1 = Raspberry Pi B rev1
  RE1 = KY-040 Rotary encoder [package=THT]

nets:
  3V3: Raspberry_Pi_B_rev1.3V3, RE1.Vcc
  GND: Raspberry_Pi_B_rev1.GND, RE1.GND
  N1: Raspberry_Pi_B_rev1.GPIO_17, RE1.CLK
  N2: Raspberry_Pi_B_rev1.GPIO_18, RE1.DT

custom parts:
  KY-040 Rotary encoder: KY-040 Rotary Encoder with switch on breakout borad from AZ Delivery
